// Logisim project Projeto.circ as structural Verilog
module somador_1bit (
  input  cin,
  input  A,
  input  B,
  output S,
  output cout
);

  wire and_1_out, and_2_out, xor_1_out;

  xor xor_1 (xor_1_out, A, B);
  and and_1 (and_1_out, A, B);
  xor xor_2 (S, cin, xor_1_out);
  and and_2 (and_2_out, cin, xor_1_out);
  or or_1 (cout, and_2_out, and_1_out);
endmodule

module somador_4bit (
  input  [3:0] B,
  input  [3:0] A,
  output Overflow,
  output [3:0] out_4
);

  wire somador_1bit_2_cout, somador_1bit_3_cout, somador_1bit_4_cout;

  somador_1bit somador_1bit_1 (.cin(somador_1bit_2_cout), .A(A[3]), .B(B[3]), .S(out_4[3]), .cout(Overflow));
  somador_1bit somador_1bit_2 (.cin(somador_1bit_3_cout), .A(A[2]), .B(B[2]), .S(out_4[2]), .cout(somador_1bit_2_cout));
  somador_1bit somador_1bit_3 (.cin(somador_1bit_4_cout), .A(A[1]), .B(B[1]), .S(out_4[1]), .cout(somador_1bit_3_cout));
  somador_1bit somador_1bit_4 (.cin(1'b0), .A(A[0]), .B(B[0]), .S(out_4[0]), .cout(somador_1bit_4_cout));
endmodule
